# Fritzing sketch Automatic Nightlight (saved by Fritzing 0.9.3b)
breadboards: 1

parts:
  Part1 = Arduino Uno (Rev3)
  R1 = Resistor [tolerance=±5% resistance=220 package="2010 [SMD]"]
  R2 = Resistor [tolerance=±5% resistance=220 package="2010 [SMD]"]
  R3 = Resistor [tolerance=±5% resistance=220 package="2010 [SMD]"]
  LED2 = RGB LED - (4 legs) [package="5 mm [THT]"]

nets:
  N1: Part1.D9_PWM, R2.Pin_1
  N2: Part1.GND, LED2.common_anode
  N3: Part1.D0/RX, R3.Pin_1
  N4: Part1.D1/TX, R1.Pin_1
  N5: R1.Pin_0, LED2.red_cathode
  N6: R2.Pin_0, LED2.blue_cathode
  N7: R3.Pin_0, LED2.green_cathode
